# Fritzing sketch 1.0 (saved by Fritzing 0.9.3b)
breadboards: 1

parts:
  Part1 = Arduino Micro (Rev3)
  S1 = Pushbutton [package="[THT]"]
  S2 = Pushbutton [package="[THT]"]
  S3 = Pushbutton [package="[THT]"]

nets:
  N1: Part1.GND, S1.Pin_1, S1.Pin_2, S2.Pin_1, S2.Pin_2, S3.Pin_1, S3.Pin_2
  N2: Part1.D6_PWM/A7, S3.Pin_3, S3.Pin_4
  N3: Part1.D9_PWM/A9, S2.Pin_3, S2.Pin_4
  N4: Part1.D12_PWM/A11, S1.Pin_3, S1.Pin_4
